# Fritzing sketch DIAGRAM (saved by Fritzing 0.9.3b)
breadboards: 1

parts:
  hc-sr1 = hc-sr04
  hc-sr2 = hc-sr04
  Part1 = Arduino Mega ADK (Rev3)
  J1 = Basic Servo
  U1 = ESP8266 WiFi Module [part_number=ESP8266]

nets:
  VCC: hc-sr1.VCC, hc-sr2.VCC, Part1.5V
  N1: hc-sr1.Trig, Part1.D12_PWM
  N2: hc-sr1.Echo, Part1.D11_PWM
  GND: hc-sr1.GND, hc-sr2.GND, Part1.GND, J1.gnd
  N3: hc-sr2.Trig, Part1.D6_PWM
  N4: hc-sr2.Echo, Part1.D5_PWM
  N5: Part1.D19/RX1, U1.GND
  N6: Part1.D18/TX1, U1.VCC
  3V3: Part1.3V3, J1.vcc, U1.RXD, U1.GPIO_2
  N7: Part1.VIN, U1.TXD
  N8: Part1.D7_PWM, J1.pulse

custom parts:
  ESP8266 WiFi Module: Generic WiFi Module based on the ESP8266 with onboard PCB antenna and UART communications
